// Logisim project cpu.circ as structural Verilog: 1 circuit, main circuit cpu
module cpu (
  input  clk,
  input  [31:0] INSTRUCTION,
  input  [31:0] READ_DATA,
  output [31:0] WRITE_ADDRESS,
  output [31:0] PROGRAM_COUNTER,
  output [31:0] ra,
  output [31:0] sp,
  output [31:0] t0,
  output [31:0] t1,
  output [31:0] t2,
  output [31:0] s0,
  output [31:0] s1,
  output [31:0] a0,
  output [31:0] tohost,
  output [3:0] WRITE_ENABLE,
  output [31:0] WRITE_DATA
);

  wire and_1_out, ASel, BrEq, BrLt, BrUn, BSel, CSRSel, CSRWen, MemRW, PCSel, RegWEn;
  wire [1:0] WBSel;
  wire [2:0] ImmSel;
  wire [3:0] ALUSel;
  wire [31:0] adder_2_out, alu_WB, imm, imm_EX, imm_MEM, imm_WB, inst_EX, inst_ID, mem_WB, multiplexer_1_out,
       multiplexer_2_out, multiplexer_3_out, PC, PC_EX, PC_ID, PC_MEM, PCadd4, PCadd4_WB, ReadData1,
       ReadData2, Result, rs1_EX, rs2_EX, WriteData;

  Adder #(.width(32)) adder_1 (.a(PROGRAM_COUNTER), .b(32'h4), .out(PCadd4));  // open: cin, cout
  Multiplexer #(.enable("false"), .width(32)) multiplexer_1 (
    .in0(PCadd4), .in1(Result), .out(multiplexer_1_out), .sel(PCSel));
  Register #(.width(32)) u_PC (.D(multiplexer_1_out), .clk(clk), .Q(PROGRAM_COUNTER));  // open: en, clr
  and and_1 (and_1_out, CSRSel, CSRWen);
  csr csr_1 (.CSR_address(12'h51e), .CSR_din(ReadData1), .CSR_WE(and_1_out), .clk(clk), .tohost(tohost));
  Register #(.width(32)) u_PC_ID (.D(PROGRAM_COUNTER), .en(1'b1), .clk(clk), .Q(PC_ID));  // open: clr
  Register #(.width(32)) u_inst_ID (.D(INSTRUCTION), .en(1'b1), .clk(clk), .Q(inst_ID));  // open: clr
  control_logic control_logic_1 (
    .inst(inst_ID), .BrEq(BrEq), .BrLt(BrLt), .PCSel(PCSel), .RegWEn(RegWEn), .ImmSel(ImmSel), .BrUn(BrUn),
    .ASel(ASel), .BSel(BSel), .ALUSel(ALUSel), .MemRW(MemRW), .WBSel(WBSel), .CSRSel(CSRSel), .CSRWen(CSRWen));
  imm_gen imm_gen_1 (.inst(inst_ID), .ImmSel(ImmSel), .imm(imm));
  regfile regfile_1 (
    .rs1(inst_ID[19:15]), .rs2(inst_ID[24:20]), .rd(inst_ID[11:7]), .Write_Data(WriteData), .RegWEn(RegWEn),
    .clk(clk), .ra(ra), .sp(sp), .t0(t0), .t1(t1), .t2(t2), .s0(s0), .s1(s1), .a0(a0),
    .Read_Data_1(ReadData1), .Read_Data_2(ReadData2));
  Register #(.width(32)) u_PC_EX (.D(PC_ID), .en(1'b1), .clk(clk), .Q(PC_EX));  // open: clr
  Register #(.width(32)) u_RS1_EX (.D(ReadData1), .en(1'b1), .clk(clk), .Q(rs1_EX));  // open: clr
  Register #(.width(32)) u_RS2_EX (.D(ReadData2), .en(1'b1), .clk(clk), .Q(rs2_EX));  // open: clr
  Register #(.width(32)) u_imm_EX (.D(imm), .en(1'b1), .clk(clk), .Q(imm_EX));  // open: clr
  Register #(.width(32)) u_inst_EX (.D(inst_ID), .en(1'b1), .clk(clk), .Q(inst_EX));  // open: clr
  branch_comp branch_comp_1 (.rs1(rs1_EX), .rs2(rs2_EX), .BrUn(BrUn), .BrEq(BrEq), .BrLt(BrLt));
  Multiplexer #(.enable("false"), .width(32)) multiplexer_2 (
    .in0(rs1_EX), .in1(PC), .out(multiplexer_2_out), .sel(ASel));
  Multiplexer #(.enable("false"), .width(32)) multiplexer_3 (
    .in0(rs2_EX), .in1(imm_EX), .out(multiplexer_3_out), .sel(BSel));
  alu alu_1 (.Result(Result), .A(multiplexer_2_out), .B(multiplexer_3_out), .ALUSel(ALUSel));
  Register #(.width(32)) u_PC_MEM (.D(PC_EX), .en(1'b1), .clk(clk), .Q(PC_MEM));  // open: clr
  Register #(.width(32)) alu_MEM (.D(Result), .en(1'b1), .clk(clk), .Q(WRITE_ADDRESS));  // open: clr
  Register #(.width(32)) rs2_MEM (.D(rs2_EX), .en(1'b1), .clk(clk), .Q(WRITE_DATA));  // open: clr
  Register #(.width(32)) u_imm_MEM (.D(inst_EX), .en(1'b1), .clk(clk), .Q(imm_MEM));  // open: clr
  assign WRITE_ENABLE = {{3{MemRW}}, MemRW};  // Bit_Extender bit_extender_1
  Adder #(.width(32)) adder_2 (.a(PC_MEM), .b(32'h4), .out(adder_2_out));  // open: cin, cout
  Register #(.width(32)) u_PCadd4_WB (.D(adder_2_out), .en(1'b1), .clk(clk), .Q(PCadd4_WB));  // open: clr
  Register #(.width(32)) u_alu_WB (.D(WRITE_ADDRESS), .en(1'b1), .clk(clk), .Q(alu_WB));  // open: clr
  Register #(.width(32)) u_mem_WB (.D(READ_DATA), .en(1'b1), .clk(clk), .Q(mem_WB));  // open: clr
  Register #(.width(32)) inst_WB (.D(imm_MEM), .en(1'b1), .clk(clk), .Q(imm_WB));  // open: clr
  Multiplexer #(.enable("false"), .select(2), .width(32)) multiplexer_4 (
    .in0(mem_WB), .in1(alu_WB), .in2(PCadd4_WB), .out(WriteData), .sel(WBSel));  // open: in3

  // Other names for the same wires on the sheet: alu_MEM[31:0] = WRITE_ADDRESS; rd[4:0] = inst_ID[11:7];
  //   rs1[4:0] = inst_ID[19:15]; rs2[4:0] = inst_ID[24:20]; rs2_MEM[31:0] = WRITE_DATA

  // Notes on the sheet:
  //   Output to IMEM
  //   IMEM (do **NOT** move this)
  //   Inputs from IMEM
  //   It is OK to move the PC, RegFile, ALU, MEM, Branch Comp, Imm Gen, and Control Logic to wherever is most convenient for you when constructing your CPU, and to delete this text
  //   Inputs/Outputs for testing. Do **NOT** move these.
  //   Outputs To DMEM
  //   DMEM (do **NOT** move this)
  //   Inputs From DMEM
endmodule
